# Fritzing sketch IoTWorkshop_Photocell (saved by Fritzing 0.9.3b)
breadboards: 1

parts:
  R6 = Resistor [tolerance=±5% resistance=10k package=THT]
  U1 = NodeMCU V1.0
  R7 = Photocell (LDR) [package=THT]
  R8 = Resistor [tolerance=±5% resistance=10k package=THT]
  LED1 = LED - 5mm [color="Red (633nm)" package="5 mm [THT]"]

nets:
  N1: R6.Pin_0, U1.A0, R7.pin_1
  N2: R6.Pin_1, U1.GND, LED1.cathode
  N3: U1.3V3, R7.pin_0
  N4: U1.D5, R8.Pin_1
  N5: R8.Pin_0, LED1.anode

notes:
  In this example, photocell values are read in through an 'Analog In' pin A0.
  The values are then used to activate an LED.
  Download the Arduino Sketch here:
  https://github.com/seattle-diy-iot/iot-workshop-photocell

custom parts:
  NodeMCU V1.0: ESP8266 based NodeMCU
